// Logisim project RiscV-32_processor.circ as structural Verilog: 19 circuits, main circuit main
module main (
  input  rst,
  output [31:0] regWr
);

  wire A_sel, B_sel, brancher_1_beq, brancher_1_bge, brancher_1_bgeu, brancher_1_blt, brancher_1_bltu,
       brancher_1_bne, clk, control_logic_1_regwrite;
  wire [1:0] WB;
  wire [2:0] control_logic_1_immsrc, r_splitter_1_func3;
  wire [3:0] control_logic_1_alusec;
  wire [4:0] r_splitter_1_rd, r_splitter_1_rs1, r_splitter_1_rs2;
  wire [6:0] r_splitter_1_func7, r_splitter_1_opcode;
  wire [25:0] pc_1_out_pc, pc_1_pcplus4;
  wire [31:0] alu_1_datad, imem_1_ins, imm_generator_1_imm, multiplexer_1_out, r1, r2;

  Clock clock_1 (.out(clk));
  pc pc_1 (.in_pc(pc_1_pcplus4), .clk(clk), .rst(rst), .pcPlus4(pc_1_pcplus4), .out_pc(pc_1_out_pc));
  IMEM imem_1 (.pc_addBy4(pc_1_out_pc[25:2]), .ins(imem_1_ins));
  R_splitter r_splitter_1 (
    .ins(imem_1_ins), .opcode(r_splitter_1_opcode), .rd(r_splitter_1_rd), .func3(r_splitter_1_func3),
    .rs1(r_splitter_1_rs1), .rs2(r_splitter_1_rs2), .func7(r_splitter_1_func7));
  control_logic control_logic_1 (
    .opcode(r_splitter_1_opcode), .func3(r_splitter_1_func3), .fn7(r_splitter_1_func7), .beq(brancher_1_beq),
    .bne(brancher_1_bne), .blt(brancher_1_blt), .bge(brancher_1_bge), .bltu(brancher_1_bltu),
    .bgeu(brancher_1_bgeu), .RegWrite(control_logic_1_regwrite), .A_sel(A_sel), .WBsel(WB),
    .immSrc(control_logic_1_immsrc), .ALUsec(control_logic_1_alusec));  // open: B_sel, memWrite, branch, memToReg, jump, PCsel
  brancher brancher_1 (
    .dataA(r1), .dataB(r2), .beq(brancher_1_beq), .bne(brancher_1_bne), .blt(brancher_1_blt),
    .bge(brancher_1_bge), .bltu(brancher_1_bltu), .bgeu(brancher_1_bgeu));
  imm_generator imm_generator_1 (.ins(imem_1_ins), .sel(control_logic_1_immsrc), .imm(imm_generator_1_imm));
  Reg_file reg_file_1 (
    .rs1_i(r_splitter_1_rs1), .rs2_i(r_splitter_1_rs2), .rd_i(r_splitter_1_rd),
    .we(control_logic_1_regwrite), .rd(regWr), .clk(clk), .rs1(r1), .rs2(r2));
  Multiplexer #(.width(32)) multiplexer_1 (.in0(r2), .in1(imm_generator_1_imm), .out(multiplexer_1_out), .sel(B_sel));
  alu alu_1 (.dataA(r1), .dataB(multiplexer_1_out), .sel(control_logic_1_alusec), .dataD(alu_1_datad));
  Multiplexer #(.select(2), .width(32)) multiplexer_2 (
    .in0(alu_1_datad), .out(regWr), .sel(WB));  // open: in1, in2, in3
endmodule

module pc (
  input  [25:0] in_pc,
  input  clk,
  input  rst,
  output [25:0] pcPlus4,
  output [25:0] out_pc
);

  Register #(.width(26)) register_1 (.D(in_pc), .en(1'b1), .clk(clk), .Q(out_pc), .clr(rst));
  Adder #(.width(26)) adder_1 (.a(out_pc), .b(26'h4), .out(pcPlus4));  // open: cin, cout

  // Other names for the same wires on the sheet: clk_t = clk; in_pc_t[25:0] = in_pc; out_pc_t[25:0] = out_pc;
  //   pcPlus4_t[25:0] = pcPlus4
endmodule

module R_splitter (
  input  [31:0] ins,
  output [6:0] opcode,
  output [4:0] rd,
  output [2:0] func3,
  output [4:0] rs1,
  output [4:0] rs2,
  output [6:0] func7
);


  assign func3 = ins[14:12];
  assign func7 = ins[31:25];
  assign opcode = ins[6:0];
  assign rd = ins[11:7];
  assign rs1 = ins[19:15];
  assign rs2 = ins[24:20];
endmodule

module i_splitter (
  input  [31:0] ins,
  output [6:0] opcode,
  output [4:0] rd,
  output [2:0] func3,
  output [4:0] rs1,
  output [11:0] imm31_20
);


  assign func3 = ins[14:12];
  assign imm31_20 = ins[31:20];
  assign opcode = ins[6:0];
  assign rd = ins[11:7];
  assign rs1 = ins[19:15];
endmodule

module s_splitter (
  input  [31:0] ins,
  output [6:0] opcode,
  output [4:0] imm4_0,
  output [2:0] func3,
  output [4:0] rs1,
  output [4:0] rs2,
  output [6:0] imm11_5
);


  assign func3 = ins[14:12];
  assign imm4_0 = ins[11:7];
  assign imm11_5 = ins[31:25];
  assign opcode = ins[6:0];
  assign rs1 = ins[19:15];
  assign rs2 = ins[24:20];
endmodule

module b_splitter (
  input  [31:0] ins,
  output [6:0] opcode,
  output imm11,
  output [3:0] imm4_1,
  output [2:0] func3,
  output [4:0] rs1,
  output [4:0] rs2,
  output [5:0] imm10_5,
  output imm12
);


  assign func3 = ins[14:12];
  assign imm4_1 = ins[11:8];
  assign imm10_5 = ins[30:25];
  assign imm11 = ins[7];
  assign imm12 = ins[31];
  assign opcode = ins[6:0];
  assign rs1 = ins[19:15];
  assign rs2 = ins[24:20];
endmodule

module u_splitter (
  input  [31:0] ins,
  output [6:0] opcode,
  output [4:0] rd,
  output [19:0] imm31_12
);


  assign imm31_12 = ins[31:12];
  assign opcode = ins[6:0];
  assign rd = ins[11:7];
endmodule

module j_splitter (
  input  [31:0] ins,
  output [6:0] opcode,
  output [4:0] rd,
  output [7:0] imm19_12,
  output imm11,
  output [9:0] imm10_1,
  output imm20
);


  assign imm10_1 = ins[30:21];
  assign imm11 = ins[20];
  assign imm19_12 = ins[19:12];
  assign imm20 = ins[31];
  assign opcode = ins[6:0];
  assign rd = ins[11:7];
endmodule

module imm_generator (
  input  [31:0] ins,
  input  [2:0] sel,
  output [31:0] imm
);

  wire [3:0] b_splitter_1_imm4_1;
  wire [4:0] s_splitter_1_imm4_0;
  wire [5:0] b_splitter_1_imm10_5;
  wire [6:0] s_splitter_1_imm11_5;
  wire [7:0] j_splitter_1_imm19_12;
  wire [9:0] j_splitter_1_imm10_1;
  wire [11:0] i_splitter_1_imm31_20;
  wire [12:11] b_splitter_1_imm11;
  wire [20:11] j_splitter_1_imm11;
  wire [31:0] Bimm_t, Iimm_t, Jimm_t, Simm_t;
  wire [31:12] Uimm_t;

  i_splitter i_splitter_1 (.ins(ins), .imm31_20(i_splitter_1_imm31_20));  // open: opcode, rd, func3, rs1
  s_splitter s_splitter_1 (
    .ins(ins), .imm4_0(s_splitter_1_imm4_0), .imm11_5(s_splitter_1_imm11_5));  // open: opcode, func3, rs1, rs2
  b_splitter b_splitter_1 (
    .ins(ins), .imm11(b_splitter_1_imm11[11]), .imm4_1(b_splitter_1_imm4_1), .imm10_5(b_splitter_1_imm10_5),
    .imm12(b_splitter_1_imm11[12]));  // open: opcode, func3, rs1, rs2
  assign Iimm_t = {{20{i_splitter_1_imm31_20[11]}}, i_splitter_1_imm31_20};  // Bit_Extender bit_extender_1
  u_splitter u_splitter_1 (.ins(ins), .imm31_12(Uimm_t));  // open: opcode, rd
  j_splitter j_splitter_1 (
    .ins(ins), .imm19_12(j_splitter_1_imm19_12), .imm11(j_splitter_1_imm11[11]),
    .imm10_1(j_splitter_1_imm10_1), .imm20(j_splitter_1_imm11[20]));  // open: opcode, rd
  assign Simm_t = {{20{s_splitter_1_imm11_5[6]}}, {s_splitter_1_imm11_5, s_splitter_1_imm4_0}};  // Bit_Extender bit_extender_2
  assign Bimm_t = {{19{b_splitter_1_imm11[12]}}, {b_splitter_1_imm11, b_splitter_1_imm10_5, b_splitter_1_imm4_1, 1'b0}};  // Bit_Extender bit_extender_3
  assign Jimm_t = {{11{j_splitter_1_imm11[20]}}, {j_splitter_1_imm11[20], j_splitter_1_imm19_12, j_splitter_1_imm11[11], j_splitter_1_imm10_1, 1'b0}};  // Bit_Extender bit_extender_4
  Multiplexer #(.select(3), .width(32)) multiplexer_1 (
    .in0(Iimm_t), .in1(Simm_t), .in2(Bimm_t), .in3(Jimm_t), .in4({Uimm_t, {12{1'b0}}}), .out(imm), .sel(sel));  // open: in5, in6, in7

  // Other names for the same wires on the sheet: imm_t[31:0] = imm; ins_t[31:0] = ins; sel_t[2:0] = sel
endmodule

module Reg_file (
  input  [4:0] rs1_i,
  input  [4:0] rs2_i,
  input  [4:0] rd_i,
  input  we,
  input  [31:0] rd,
  input  clk,
  output [31:0] rs1,
  output [31:0] rs2
);

  wire r0_wet, r1_wet, r2_wet, r3_wet, r4_wet, r5_wet, r6_wet, r7_wet, r8_wet, r9_wet, r10_wet, r11_wet,
       r12_wet, r13_wet, r14_wet, r15_wet, r16_wet, r17_wet, r18_wet, r19_wet, r20_wet, r21_wet, r22_wet,
       r23_wet, r24_wet, r25_wet, r26_wet, r27_wet, r28_wet, r29_wet, r30_wet, r31_wet;
  wire [31:0] d_x1, d_x2, d_x3, d_x4, d_x5, d_x6, d_x7, d_x8, d_x9, d_x10, d_x11, d_x12, d_x13, d_x14, d_x15,
       d_x16, d_x17, d_x18, d_x19, d_x20, d_x21, d_x22, d_x23, d_x24, d_x25, d_x26, d_x27, d_x28, d_x29,
       d_x30, d_x31;

  Decoder #(.select(5)) decoder_1 (
    .out0(r0_wet), .out1(r1_wet), .out2(r2_wet), .out3(r3_wet), .out4(r4_wet), .out5(r5_wet), .out6(r6_wet),
    .out7(r7_wet), .out8(r8_wet), .out9(r9_wet), .out10(r10_wet), .out11(r11_wet), .out12(r12_wet),
    .out13(r13_wet), .out14(r14_wet), .out15(r15_wet), .out16(r16_wet), .out17(r17_wet), .out18(r18_wet),
    .out19(r19_wet), .out20(r20_wet), .out21(r21_wet), .out22(r22_wet), .out23(r23_wet), .out24(r24_wet),
    .out25(r25_wet), .out26(r26_wet), .out27(r27_wet), .out28(r28_wet), .out29(r29_wet), .out30(r30_wet),
    .out31(r31_wet), .sel(rd_i), .en(we));
  Register #(.width(32)) x4 (.D(rd), .en(r4_wet), .clk(clk), .Q(d_x4));  // open: clr
  Register #(.width(32)) x8 (.D(rd), .en(r8_wet), .clk(clk), .Q(d_x8));  // open: clr
  Register #(.width(32)) x12 (.D(rd), .en(r12_wet), .clk(clk), .Q(d_x12));  // open: clr
  Register #(.width(32)) x16 (.D(rd), .en(r16_wet), .clk(clk), .Q(d_x16));  // open: clr
  Register #(.width(32)) x20 (.D(rd), .en(r20_wet), .clk(clk), .Q(d_x20));  // open: clr
  Register #(.width(32)) x24 (.D(rd), .en(r24_wet), .clk(clk), .Q(d_x24));  // open: clr
  Register #(.width(32)) x28 (.D(rd), .en(r28_wet), .clk(clk), .Q(d_x28));  // open: clr
  Register #(.width(32)) x1 (.D(rd), .en(r1_wet), .clk(clk), .Q(d_x1));  // open: clr
  Register #(.width(32)) x5 (.D(rd), .en(r5_wet), .clk(clk), .Q(d_x5));  // open: clr
  Register #(.width(32)) x9 (.D(rd), .en(r9_wet), .clk(clk), .Q(d_x9));  // open: clr
  Register #(.width(32)) x13 (.D(rd), .en(r13_wet), .clk(clk), .Q(d_x13));  // open: clr
  Register #(.width(32)) x17 (.D(rd), .en(r17_wet), .clk(clk), .Q(d_x17));  // open: clr
  Register #(.width(32)) x21 (.D(rd), .en(r21_wet), .clk(clk), .Q(d_x21));  // open: clr
  Register #(.width(32)) x25 (.D(rd), .en(r25_wet), .clk(clk), .Q(d_x25));  // open: clr
  Register #(.width(32)) x29 (.D(rd), .en(r29_wet), .clk(clk), .Q(d_x29));  // open: clr
  Register #(.width(32)) x2 (.D(rd), .en(r2_wet), .clk(clk), .Q(d_x2));  // open: clr
  Register #(.width(32)) x6 (.D(rd), .en(r6_wet), .clk(clk), .Q(d_x6));  // open: clr
  Register #(.width(32)) x10 (.D(rd), .en(r10_wet), .clk(clk), .Q(d_x10));  // open: clr
  Register #(.width(32)) x14 (.D(rd), .en(r14_wet), .clk(clk), .Q(d_x14));  // open: clr
  Register #(.width(32)) x18 (.D(rd), .en(r18_wet), .clk(clk), .Q(d_x18));  // open: clr
  Register #(.width(32)) x22 (.D(rd), .en(r22_wet), .clk(clk), .Q(d_x22));  // open: clr
  Register #(.width(32)) x26 (.D(rd), .en(r26_wet), .clk(clk), .Q(d_x26));  // open: clr
  Register #(.width(32)) x30 (.D(rd), .en(r30_wet), .clk(clk), .Q(d_x30));  // open: clr
  Register #(.width(32)) x3 (.D(rd), .en(r3_wet), .clk(clk), .Q(d_x3));  // open: clr
  Register #(.width(32)) x7 (.D(rd), .en(r7_wet), .clk(clk), .Q(d_x7));  // open: clr
  Register #(.width(32)) x11 (.D(rd), .en(r11_wet), .clk(clk), .Q(d_x11));  // open: clr
  Register #(.width(32)) x15 (.D(rd), .en(r15_wet), .clk(clk), .Q(d_x15));  // open: clr
  Register #(.width(32)) x19 (.D(rd), .en(r19_wet), .clk(clk), .Q(d_x19));  // open: clr
  Register #(.width(32)) x23 (.D(rd), .en(r23_wet), .clk(clk), .Q(d_x23));  // open: clr
  Register #(.width(32)) x27 (.D(rd), .en(r27_wet), .clk(clk), .Q(d_x27));  // open: clr
  Register #(.width(32)) x31 (.D(rd), .en(r31_wet), .clk(clk), .Q(d_x31));  // open: clr
  Multiplexer #(.select(5), .width(32)) multiplexer_1 (
    .in0({32{1'b0}}), .in1(d_x1), .in2(d_x2), .in3(d_x3), .in4(d_x4), .in5(d_x5), .in6(d_x6), .in7(d_x7),
    .in8(d_x8), .in9(d_x9), .in10(d_x10), .in11(d_x11), .in12(d_x12), .in13(d_x13), .in14(d_x14),
    .in15(d_x15), .in16(d_x16), .in17(d_x17), .in18(d_x18), .in19(d_x19), .in20(d_x20), .in21(d_x21),
    .in22(d_x22), .in23(d_x23), .in24(d_x24), .in25(d_x25), .in26(d_x26), .in27(d_x27), .in28(d_x28),
    .in29(d_x29), .in30(d_x30), .in31(d_x31), .out(rs1), .sel(rs1_i));
  Multiplexer #(.select(5), .width(32)) multiplexer_2 (
    .in0({32{1'b0}}), .in1(d_x1), .in2(d_x2), .in3(d_x3), .in4(d_x4), .in5(d_x5), .in6(d_x6), .in7(d_x7),
    .in8(d_x8), .in9(d_x9), .in10(d_x10), .in11(d_x11), .in12(d_x12), .in13(d_x13), .in14(d_x14),
    .in15(d_x15), .in16(d_x16), .in17(d_x17), .in18(d_x18), .in19(d_x19), .in20(d_x20), .in21(d_x21),
    .in22(d_x22), .in23(d_x23), .in24(d_x24), .in25(d_x25), .in26(d_x26), .in27(d_x27), .in28(d_x28),
    .in29(d_x29), .in30(d_x30), .in31(d_x31), .out(rs2), .sel(rs2_i));

  // Other names for the same wires on the sheet: rd_i_t[4:0] = rd_i; rd_t[31:0] = rd; rs1_i_t[4:0] = rs1_i;
  //   rs1_t[31:0] = rs1; rs2_i_t[4:0] = rs2_i; rs2_t[31:0] = rs2; we_t = we
endmodule

module brancher (
  input  [31:0] dataA,
  input  [31:0] dataB,
  output beq,
  output bne,
  output blt,
  output bge,
  output bltu,
  output bgeu
);

  Comparator #(.width(32)) comparator_1 (.a(dataA), .b(dataB), .eq(beq), .lt(blt));  // open: gt
  Comparator #(.mode("unsigned"), .width(32)) comparator_2 (.a(dataA), .b(dataB), .lt(bltu));  // open: gt, eq
  not not_1 (bne, beq);
  not not_2 (bge, blt);
  not not_3 (bgeu, bltu);

  // Other names for the same wires on the sheet: beq_t = beq; blt_t = blt; bltu_t = bltu; dataA_t[31:0] = dataA;
  //   dataB_t[31:0] = dataB
endmodule

module alu (
  input  [31:0] dataA,
  input  [31:0] dataB,
  input  [3:0] sel,
  output [31:0] dataD
);

  wire comparator_1_lt, comparator_2_lt;
  wire [31:0] add_out, and_out, or_out, sll_out, slt_out, sltu_out, sra_out, srl_out, sub_out, xor_out;

  Adder #(.width(32)) adder_1 (.a(dataA), .b(dataB), .out(add_out));  // open: cin, cout
  Subtractor #(.width(32)) subtractor_1 (.a(dataA), .b(dataB), .out(sub_out));  // open: bin, bout
  Shifter #(.width(32)) shifter_1 (.in(dataA), .\dist (dataB[4:0]), .out(sll_out));
  Comparator #(.width(32)) comparator_1 (.a(dataA), .b(dataB), .lt(comparator_1_lt));  // open: gt, eq
  Comparator #(.mode("unsigned"), .width(32)) comparator_2 (
    .a(dataA), .b(dataB), .lt(comparator_2_lt));  // open: gt, eq
  assign xor_out = dataA ^ dataB;  // XOR_Gate xor_1, 32 bits wide
  Shifter #(.shift("lr"), .width(32)) shifter_2 (.in(dataA), .\dist (dataB[4:0]), .out(srl_out));
  Shifter #(.shift("ar"), .width(32)) shifter_3 (.in(dataA), .\dist (dataB[4:0]), .out(sra_out));
  assign or_out = dataA | dataB;  // OR_Gate or_1, 32 bits wide
  assign and_out = dataA & dataB;  // AND_Gate and_1, 32 bits wide
  assign slt_out = {{31{1'b0}}, comparator_1_lt};  // Bit_Extender bit_extender_1
  assign sltu_out = {{31{1'b0}}, comparator_2_lt};  // Bit_Extender bit_extender_2
  Multiplexer #(.select(4), .width(32)) multiplexer_1 (
    .in0(add_out), .in1(sll_out), .in2(slt_out), .in3(sltu_out), .in4(xor_out), .in5(srl_out), .in6(or_out),
    .in7(and_out), .in8(sub_out), .in13(sra_out), .in15(dataB), .out(dataD), .sel(sel));  // open: in9, in10, in11, in12, in14

  // Other names for the same wires on the sheet: dataA_t[31:0] = dataA; dataB_L5_t[4:0] = dataB[4:0];
  //   dataB_t[31:0] = dataB; dataD_t[31:0] = dataD; sel_t[3:0] = sel
endmodule

module control_unit (
  output [31:0] out32
);

  wire clock_1_out, control_1_regwena;
  wire [3:0] control_1_alusel;
  wire [4:0] r_splitter_1_rd, r_splitter_1_rs1, r_splitter_1_rs2;
  wire [31:0] reg_file_1_rs1, reg_file_1_rs2;

  R_splitter r_splitter_1 (
    .ins(32'h418133), .rd(r_splitter_1_rd), .rs1(r_splitter_1_rs1), .rs2(r_splitter_1_rs2));  // open: opcode, func3, func7
  Clock clock_1 (.out(clock_1_out));
  Reg_file reg_file_1 (
    .rs1_i(r_splitter_1_rs1), .rs2_i(r_splitter_1_rs2), .rd_i(r_splitter_1_rd), .we(control_1_regwena),
    .rd(out32), .clk(clock_1_out), .rs1(reg_file_1_rs1), .rs2(reg_file_1_rs2));
  control control_1 (.ins(32'h418133), .aluSel(control_1_alusel), .regwena(control_1_regwena));
  alu alu_1 (.dataA(reg_file_1_rs1), .dataB(reg_file_1_rs2), .sel(control_1_alusel), .dataD(out32));
endmodule

module control (
  input  [31:0] ins,
  output [3:0] aluSel,
  output regwena
);

  wire add_t, or_t;

  and and_1 (add_t, ~ins[2], ~ins[3], ins[4], ins[5], ~ins[6], ~ins[13], ~ins[14], ins[15], ~ins[30]);  // AND_Gate
  and and_2 (aluSel[3], ~ins[2], ~ins[3], ins[4], ins[5], ~ins[6], ~ins[13], ~ins[14], ~ins[15], ins[30]);  // AND_Gate
  and and_3 (or_t, ~ins[2], ~ins[3], ins[4], ins[5], ~ins[6], ~ins[13], ins[14], ins[15], ~ins[30]);  // AND_Gate
  and and_4 (aluSel[0], ~ins[2], ~ins[3], ins[4], ins[5], ~ins[6], ins[13], ins[14], ins[15], ~ins[30]);  // AND_Gate
  or or_1 (aluSel[2], or_t, aluSel[0]);
  or or_2 (regwena, aluSel[3], aluSel[0], add_t, or_t);

  assign aluSel[1] = aluSel[2];

  // Other names for the same wires on the sheet: and_t = aluSel[0]; as0_t = aluSel[0]; as1_t = aluSel[2];
  //   as2_t = aluSel[2]; as3_t = aluSel[3]; sub_t = aluSel[3]; i2_t = ins[2]; i3_t = ins[3]; i4_t = ins[4];
  //   i5_t = ins[5]; i6_t = ins[6]; i12_t = ins[13]; i13_t = ins[14]; i14_t = ins[15]; i30_t = ins[30]
endmodule

module IMEM (
  input  [23:0] pc_addBy4,
  output [31:0] ins
);

  ROM #(.addrWidth(24), .dataWidth(32)) rom_1 (.addr(pc_addBy4), .data(ins));

  // Notes on the sheet:
  //   contents of rom_1 (hex, n*v repeats v):
  //   a00093 500113 2081b3 302423 802203 418263 6300293 fe5ff06f
endmodule

module control_logic (
  input  [6:0] opcode,
  input  [2:0] func3,
  input  [6:0] fn7,
  input  beq,
  input  bne,
  input  blt,
  input  bge,
  input  bltu,
  input  bgeu,
  output RegWrite,
  output B_sel,
  output memWrite,
  output branch,
  output A_sel,
  output memToReg,
  output jump,
  output [1:0] WBsel,
  output [2:0] immSrc,
  output PCsel,
  output [3:0] ALUsec
);

  wire and_1_out, and_11_out, and_12_out, and_13_out, auipc_type, branch_taken, f3n000, f3n001, f3n010,
       f3n011, f3n100, f3n101, f3n110, f3n111, I_type, isAdd, isand, islui, isor, isSll, isSlt, isSltu,
       isSra, isSrl, isSub, isxor, jalr_type, multiplexer_1_out, or_6_out, or_7_out, R_type;

  and and_1 (and_1_out, branch_taken, branch);
  Multiplexer #(.select(3)) multiplexer_1 (
    .in0(beq), .in1(bne), .in4(blt), .in5(bge), .in6(bltu), .in7(bgeu), .out(multiplexer_1_out), .sel(func3));  // open: in2, in3
  Comparator #(.width(7)) comparator_1 (.a(7'b0110011), .b(opcode), .eq(R_type));  // open: gt, lt
  Comparator #(.width(7)) comparator_2 (.a(7'b0010011), .b(opcode), .eq(I_type));  // open: gt, lt
  Comparator #(.width(7)) comparator_3 (.a(7'b0000011), .b(opcode), .eq(memToReg));  // open: gt, lt
  Comparator #(.width(7)) comparator_4 (.a(7'b0100011), .b(opcode), .eq(branch));  // open: gt, lt
  Comparator #(.width(7)) comparator_5 (.a(7'b1100011), .b(opcode), .eq(branch));  // open: gt, lt
  Comparator #(.width(7)) comparator_6 (.a(7'b1101111), .b(opcode), .eq(immSrc[2]));  // open: gt, lt
  Comparator #(.width(7)) comparator_7 (.a(7'b0110111), .b(opcode), .eq(islui));  // open: gt, lt
  Comparator #(.width(7)) comparator_8 (.a(7'b1100111), .b(opcode), .eq(jalr_type));  // open: gt, lt
  Comparator #(.width(7)) comparator_9 (.a(7'b0010111), .b(opcode), .eq(auipc_type));  // open: gt, lt
  or or_1 (PCsel, and_1_out, immSrc[2], jalr_type);
  and and_2 (branch_taken, multiplexer_1_out, branch);
  and and_3 (f3n000, ~func3[0], ~func3[1], ~func3[2]);  // AND_Gate
  and and_4 (f3n001, func3[0], ~func3[1], ~func3[2]);  // AND_Gate
  and and_5 (f3n010, ~func3[0], func3[1], ~func3[2]);  // AND_Gate
  and and_6 (f3n011, func3[0], func3[1], ~func3[2]);  // AND_Gate
  and and_7 (f3n100, ~func3[0], ~func3[1], func3[2]);  // AND_Gate
  and and_8 (f3n101, func3[0], ~func3[1], func3[2]);  // AND_Gate
  and and_9 (f3n110, ~func3[0], func3[1], func3[2]);  // AND_Gate
  and and_10 (f3n111, func3[0], func3[1], func3[2]);
  or or_2 (jump, immSrc[2], jalr_type);
  or or_3 (immSrc[0], branch, islui, auipc_type);
  or or_4 (immSrc[1], branch, islui, auipc_type);
  or or_5 (RegWrite, jalr_type, R_type, I_type, auipc_type, immSrc[2], islui, memToReg);
  and and_11 (and_11_out, R_type, fn7[5]);
  or or_6 (or_6_out, and_11_out, I_type);
  or or_7 (or_7_out, I_type, R_type);
  and and_12 (and_12_out, or_6_out, f3n000);
  and and_13 (and_13_out, R_type, f3n000, fn7[5]);
  or or_8 (isAdd, auipc_type, branch, and_12_out, memToReg);
  or or_9 (isSub, and_13_out, branch);
  and and_14 (isSll, f3n001, or_7_out);
  and and_15 (isSlt, f3n010, or_7_out);
  and and_16 (isSltu, f3n011, or_7_out);
  and and_17 (isxor, f3n100, or_7_out);
  and and_18 (isSrl, f3n101, ~fn7[5], or_7_out);  // AND_Gate
  and and_19 (isSra, f3n101, fn7[5], or_7_out);
  and and_20 (isor, f3n110, or_7_out);
  and and_21 (isand, f3n111, or_7_out);
  or or_10 (B_sel, branch, branch, jalr_type, I_type, immSrc[2], islui, memToReg, auipc_type);
  or or_11 (A_sel, branch, immSrc[2], auipc_type);
  or or_12 (WBsel[1], jalr_type, immSrc[2]);
  or or_13 (ALUsec[0], isSll, isSltu, isSrl, isSra, isand, islui);
  or or_14 (ALUsec[1], isSlt, isSltu, isor, isand, islui);
  or or_15 (ALUsec[2], isxor, isSrl, isSra, isor, isand, islui);
  or or_16 (ALUsec[3], isSub, isSra, islui);

  assign memWrite = branch;
  assign WBsel[0] = memToReg;

  // Other names for the same wires on the sheet: f7_5 = fn7[5]; f3n0 = func3[0]; fun3[2:0] = func3; f3n1 = func3[1];
  //   f3n2 = func3[2]; jal_type = immSrc[2]; lui_type = islui; B_type = branch; store_type = branch;
  //   Load_type = memToReg
endmodule

module dmem (
  input  [31:0] AddressIn_byalu,
  input  store,
  input  clock,
  input  [31:0] valueToStore,
  output [31:0] dmemOut
);

  wire not_1_out;

  RAM #(.addrWidth(10), .dataWidth(32)) dmem (
    .addr(AddressIn_byalu[11:2]), .we(store), .oe(not_1_out), .clk(clock), .din(valueToStore), .dout(dmemOut));
  not not_1 (not_1_out, store);
endmodule

module processor (
);

  wire clk, control_logic_1_p1, r_splitter_1_p2, r_splitter_1_p4, r_splitter_1_p7;
  wire [3:0] control_logic_1_p5;
  wire [4:0] r_splitter_1_p3, r_splitter_1_p5, r_splitter_1_p6;
  wire [25:0] pc_1_out_pc, pc_1_pcplus4;
  wire [31:0] alu_1_datad, imem_1_ins, reg_file_1_rs1, reg_file_1_rs2;

  Clock clock_1 (.out(clk));
  pc pc_1 (.in_pc(pc_1_pcplus4), .clk(clk), .pcPlus4(pc_1_pcplus4), .out_pc(pc_1_out_pc));  // open: rst
  IMEM imem_1 (.pc_addBy4(pc_1_out_pc[25:2]), .ins(imem_1_ins));
  // R_splitter r_splitter_1: pin names not known; wires that end beside it: imem_1_ins, r_splitter_1_p2, r_splitter_1_p3, r_splitter_1_p4, r_splitter_1_p5, r_splitter_1_p6, r_splitter_1_p7
  // control_logic control_logic_1: pin names not known; wires that end beside it: control_logic_1_p1, r_splitter_1_p2, r_splitter_1_p4, r_splitter_1_p7, control_logic_1_p5
  Reg_file reg_file_1 (
    .rs1_i(r_splitter_1_p5), .rs2_i(r_splitter_1_p6), .rd_i(r_splitter_1_p3), .we(control_logic_1_p1),
    .rd(alu_1_datad), .clk(clk), .rs1(reg_file_1_rs1), .rs2(reg_file_1_rs2));
  alu alu_1 (.dataA(reg_file_1_rs1), .dataB(reg_file_1_rs2), .sel(control_logic_1_p5), .dataD(alu_1_datad));
endmodule

module Regfile1 (
  input  [4:0] Readreg1,
  input  [4:0] Readreg2,
  input  [4:0] WriteReg,
  input  [31:0] WriteData,
  input  RegWrite,
  input  Clk,
  output [31:0] ReadData1,
  output [31:0] ReadData2
);

  wire comparator_1_gt, comparator_2_gt, decoder_1_out1, decoder_1_out2, decoder_1_out3, decoder_1_out4,
       decoder_1_out5, decoder_1_out6, decoder_1_out7, decoder_1_out8, decoder_1_out9, decoder_1_out10,
       decoder_1_out11, decoder_1_out12, decoder_1_out13, decoder_1_out14, decoder_1_out15, decoder_1_out16,
       decoder_1_out17, decoder_1_out18, decoder_1_out19, decoder_1_out20, decoder_1_out21, decoder_1_out22,
       decoder_1_out23, decoder_1_out24, decoder_1_out25, decoder_1_out26, decoder_1_out27, decoder_1_out28,
       decoder_1_out29, decoder_1_out30, decoder_1_out31;
  wire [31:0] multiplexer_1_out, multiplexer_2_out, register_1_q, register_2_q, register_3_q, register_4_q,
       register_5_q, register_6_q, register_7_q, register_8_q, register_9_q, register_10_q, register_11_q,
       register_12_q, register_13_q, register_14_q, register_15_q, register_16_q, register_17_q,
       register_18_q, register_19_q, register_20_q, register_21_q, register_22_q, register_23_q,
       register_24_q, register_25_q, register_26_q, register_27_q, register_28_q, register_29_q,
       register_30_q, register_31_q;

  Decoder #(.select(5)) decoder_1 (
    .out1(decoder_1_out1), .out2(decoder_1_out2), .out3(decoder_1_out3), .out4(decoder_1_out4),
    .out5(decoder_1_out5), .out6(decoder_1_out6), .out7(decoder_1_out7), .out8(decoder_1_out8),
    .out9(decoder_1_out9), .out10(decoder_1_out10), .out11(decoder_1_out11), .out12(decoder_1_out12),
    .out13(decoder_1_out13), .out14(decoder_1_out14), .out15(decoder_1_out15), .out16(decoder_1_out16),
    .out17(decoder_1_out17), .out18(decoder_1_out18), .out19(decoder_1_out19), .out20(decoder_1_out20),
    .out21(decoder_1_out21), .out22(decoder_1_out22), .out23(decoder_1_out23), .out24(decoder_1_out24),
    .out25(decoder_1_out25), .out26(decoder_1_out26), .out27(decoder_1_out27), .out28(decoder_1_out28),
    .out29(decoder_1_out29), .out30(decoder_1_out30), .out31(decoder_1_out31), .sel(WriteReg), .en(RegWrite));  // open: out0
  Register #(.width(32)) register_1 (.D(WriteData), .en(decoder_1_out1), .clk(Clk), .Q(register_1_q));  // open: clr
  Register #(.width(32)) register_2 (.D(WriteData), .en(decoder_1_out2), .clk(Clk), .Q(register_2_q));  // open: clr
  Register #(.width(32)) register_3 (.D(WriteData), .en(decoder_1_out3), .clk(Clk), .Q(register_3_q));  // open: clr
  Register #(.width(32)) register_4 (.D(WriteData), .en(decoder_1_out4), .clk(Clk), .Q(register_4_q));  // open: clr
  Register #(.width(32)) register_5 (.D(WriteData), .en(decoder_1_out5), .clk(Clk), .Q(register_5_q));  // open: clr
  Register #(.width(32)) register_6 (.D(WriteData), .en(decoder_1_out6), .clk(Clk), .Q(register_6_q));  // open: clr
  Register #(.width(32)) register_7 (.D(WriteData), .en(decoder_1_out7), .clk(Clk), .Q(register_7_q));  // open: clr
  Register #(.width(32)) register_8 (.D(WriteData), .en(decoder_1_out8), .clk(Clk), .Q(register_8_q));  // open: clr
  Register #(.width(32)) register_9 (.D(WriteData), .en(decoder_1_out9), .clk(Clk), .Q(register_9_q));  // open: clr
  Register #(.width(32)) register_10 (.D(WriteData), .en(decoder_1_out10), .clk(Clk), .Q(register_10_q));  // open: clr
  Register #(.width(32)) register_11 (.D(WriteData), .en(decoder_1_out11), .clk(Clk), .Q(register_11_q));  // open: clr
  Register #(.width(32)) register_12 (.D(WriteData), .en(decoder_1_out12), .clk(Clk), .Q(register_12_q));  // open: clr
  Register #(.width(32)) register_13 (.D(WriteData), .en(decoder_1_out13), .clk(Clk), .Q(register_13_q));  // open: clr
  Register #(.width(32)) register_14 (.D(WriteData), .en(decoder_1_out14), .clk(Clk), .Q(register_14_q));  // open: clr
  Register #(.width(32)) register_15 (.D(WriteData), .en(decoder_1_out15), .clk(Clk), .Q(register_15_q));  // open: clr
  Register #(.width(32)) register_16 (.D(WriteData), .en(decoder_1_out16), .clk(Clk), .Q(register_16_q));  // open: clr
  Register #(.width(32)) register_17 (.D(WriteData), .en(decoder_1_out17), .clk(Clk), .Q(register_17_q));  // open: clr
  Register #(.width(32)) register_18 (.D(WriteData), .en(decoder_1_out18), .clk(Clk), .Q(register_18_q));  // open: clr
  Register #(.width(32)) register_19 (.D(WriteData), .en(decoder_1_out19), .clk(Clk), .Q(register_19_q));  // open: clr
  Register #(.width(32)) register_20 (.D(WriteData), .en(decoder_1_out20), .clk(Clk), .Q(register_20_q));  // open: clr
  Register #(.width(32)) register_21 (.D(WriteData), .en(decoder_1_out21), .clk(Clk), .Q(register_21_q));  // open: clr
  Register #(.width(32)) register_22 (.D(WriteData), .en(decoder_1_out22), .clk(Clk), .Q(register_22_q));  // open: clr
  Register #(.width(32)) register_23 (.D(WriteData), .en(decoder_1_out23), .clk(Clk), .Q(register_23_q));  // open: clr
  Register #(.width(32)) register_24 (.D(WriteData), .en(decoder_1_out24), .clk(Clk), .Q(register_24_q));  // open: clr
  Register #(.width(32)) register_25 (.D(WriteData), .en(decoder_1_out25), .clk(Clk), .Q(register_25_q));  // open: clr
  Register #(.width(32)) register_26 (.D(WriteData), .en(decoder_1_out26), .clk(Clk), .Q(register_26_q));  // open: clr
  Register #(.width(32)) register_27 (.D(WriteData), .en(decoder_1_out27), .clk(Clk), .Q(register_27_q));  // open: clr
  Register #(.width(32)) register_28 (.D(WriteData), .en(decoder_1_out28), .clk(Clk), .Q(register_28_q));  // open: clr
  Register #(.width(32)) register_29 (.D(WriteData), .en(decoder_1_out29), .clk(Clk), .Q(register_29_q));  // open: clr
  Register #(.width(32)) register_30 (.D(WriteData), .en(decoder_1_out30), .clk(Clk), .Q(register_30_q));  // open: clr
  Register #(.width(32)) register_31 (.D(WriteData), .en(decoder_1_out31), .clk(Clk), .Q(register_31_q));  // open: clr
  Multiplexer #(.select(5), .width(32)) multiplexer_1 (
    .in0({32{1'b0}}), .in1(register_1_q), .in2(register_2_q), .in3(register_3_q), .in4(register_4_q),
    .in5(register_5_q), .in6(register_6_q), .in7(register_7_q), .in8(register_8_q), .in9(register_9_q),
    .in10(register_10_q), .in11(register_11_q), .in12(register_12_q), .in13(register_13_q),
    .in14(register_14_q), .in15(register_15_q), .in16(register_16_q), .in17(register_17_q),
    .in18(register_18_q), .in19(register_19_q), .in20(register_20_q), .in21(register_21_q),
    .in22(register_22_q), .in23(register_23_q), .in24(register_24_q), .in25(register_25_q),
    .in26(register_26_q), .in27(register_27_q), .in28(register_28_q), .in29(register_29_q),
    .in30(register_30_q), .in31(register_31_q), .out(multiplexer_1_out), .sel(Readreg1));
  Multiplexer #(.select(5), .width(32)) multiplexer_2 (
    .in0({32{1'b0}}), .in1(register_1_q), .in2(register_2_q), .in3(register_3_q), .in4(register_4_q),
    .in5(register_5_q), .in6(register_6_q), .in7(register_7_q), .in8(register_8_q), .in9(register_9_q),
    .in10(register_10_q), .in11(register_11_q), .in12(register_12_q), .in13(register_13_q),
    .in14(register_14_q), .in15(register_15_q), .in16(register_16_q), .in17(register_17_q),
    .in18(register_18_q), .in19(register_19_q), .in20(register_20_q), .in21(register_21_q),
    .in22(register_22_q), .in23(register_23_q), .in24(register_24_q), .in25(register_25_q),
    .in26(register_26_q), .in27(register_27_q), .in28(register_28_q), .in29(register_29_q),
    .in30(register_30_q), .in31(register_31_q), .out(multiplexer_2_out), .sel(Readreg2));
  Multiplexer #(.width(32)) multiplexer_3 (
    .in0({32{1'b0}}), .in1(multiplexer_2_out), .out(ReadData2), .sel(comparator_2_gt));
  Multiplexer #(.width(32)) multiplexer_4 (
    .in0({32{1'b0}}), .in1(multiplexer_1_out), .out(ReadData1), .sel(comparator_1_gt));
  Comparator #(.mode("unsigned"), .width(5)) comparator_1 (
    .a(Readreg1), .b({5{1'b0}}), .gt(comparator_1_gt));  // open: eq, lt
  Comparator #(.mode("unsigned"), .width(5)) comparator_2 (
    .a(Readreg2), .b({5{1'b0}}), .gt(comparator_2_gt));  // open: eq, lt
endmodule
